# Fritzing sketch sumo bot wiring (saved by Fritzing 0.9.3b)
breadboards: 1

parts:
  Part1 = Arduino Uno (Rev3)
  hc-sr1 = hc-sr04
  hc-sr2 = hc-sr04
  hc-sr3 = hc-sr04
  hc-sr4 = hc-sr04
  hc-sr5 = hc-sr04
  M1 = DC Motor
  M2 = DC Motor
  IC1 = H-Bridge [package=THT]
  U1 = QRD1114 [package=qrd1114]
  U2 = QRD1114 [package=qrd1114]
  U3 = QRD1114 [package=qrd1114]
  U4 = QRD1114 [package=qrd1114]
  R1 = Resistor [tolerance=±5% resistance=470 package="0402 [SMD]"]
  R2 = Resistor [tolerance=±5% resistance=470 package="0402 [SMD]"]
  R4 = Resistor [tolerance=±5% resistance=470 package="0402 [SMD]"]
  R10 = Resistor [tolerance=±5% resistance=4.7k package="0402 [SMD]"]
  R11 = Resistor [tolerance=±5% resistance=4.7k package="0402 [SMD]"]
  R14 = Resistor [tolerance=±5% resistance=470 package="0402 [SMD]"]  # not connected
  R15 = Resistor [tolerance=±5% resistance=470 package="0402 [SMD]"]
  R16 = Resistor [tolerance=±5% resistance=4.7k package="0402 [SMD]"]
  R17 = Resistor [tolerance=±5% resistance=4.7k package="0402 [SMD]"]

nets:
  N1: Part1.D9_PWM, U1.K
  N2: Part1.D10_PWM/SS, U2.K
  N3: Part1.D11_PWM/MOSI, U3.K
  N4: Part1.D12/MISO, U4.K
  GND: Part1.GND, hc-sr1.GND, hc-sr2.GND, hc-sr3.GND, hc-sr4.GND, hc-sr5.GND, IC1.GND1, IC1.GND2, IC1.GND3, IC1.GND4, U1.C, U2.C, U3.C, U4.C
  N5: Part1.D2, IC1.2A
  N6: Part1.D3_PWM, IC1.1A
  N7: Part1.D4, IC1.3A
  N8: Part1.D5_PWM, IC1.4A
  VCC: Part1.5V, hc-sr1.VCC, hc-sr2.VCC, hc-sr3.VCC, hc-sr5.VCC, IC1.1_2EN, IC1.VCC2, IC1.3_4EN, IC1.VCC1, R1.Pin_0, R2.Pin_0, R4.Pin_0, R10.Pin_0, R11.Pin_0, R15.Pin_0, R16.Pin_0, R17.Pin_0
  N9: M1.pin_1, IC1.1Y
  N10: M1.pin_2, IC1.2Y
  N11: M2.pin_1, IC1.4Y
  N12: M2.pin_2, IC1.3Y
  N13: U1.E, R10.Pin_1
  N14: U1.A, R1.Pin_1
  N15: U2.E, R17.Pin_1
  N16: U2.A, R2.Pin_1
  N17: U3.E, R11.Pin_1
  N18: U3.A, R4.Pin_1
  N19: U4.E, R16.Pin_1
  N20: U4.A, R15.Pin_1
